// Digital circuit ejer1.dig as structural Verilog
module ejer1 (
);

  wire [9:0] undriven;

  ROM #(.AddrBits(10), .Bits(32)) CacheMem (.A(undriven));  // open: sel, D
  Comparator comparator_1 (.a(undriven[0]));  // open: b, gt, eq, lt
  Comparator comparator_2 (.a(undriven[0]));  // open: b, gt, eq, lt
  Comparator comparator_3 (.a(undriven[0]));  // open: b, gt, eq, lt
  // Pins of 1 and 10 bits meet at undriven
endmodule
